# Fritzing sketch amp_circuit (saved by Fritzing 0.9.3b)
breadboards: 1

parts:
  Part2 = TFT 1.8 inch 160x128 w microSD [part_number=358]  # not connected
  Part3 = Adafruit MAX98357A I2S 3W Class D Amplifier [part_number="Adafruit #3006"]
  U1 = LIPO-2000mAh [package=lipo-2000]
  ENCODER1 = Rotary Encoder with Knob  # not connected
  ENCODER2 = Rotary Encoder with Knob  # not connected
  SP1 = SPEAKER [package=pcb_mount_speaker]
  Part4 = USB LiPoly Charger

nets:
  N1: Part3.VO-, SP1.+
  N2: Part3.VO+, SP1.-
  N3: U1.+, Part4.VBAT
  N4: U1.-, Part4.GND

custom parts:
  TFT 1.8 inch 160x128 w microSD: This lovely little display breakout is the best way to add a small, colorful and bright display to any project. Since the display uses 4-wire SPI to communicate and has its own pixel-addressable frame buffer, it can be used with every kind of microcontroller. Even a very small one with low memory and few pins available! The 1.8" display has 128x160 color pixels.
  Adafruit MAX98357A I2S 3W Class D Amplifier: Listen to this good news - we now have an all in one digital audio amp breakout board that works incredibly well with the Raspberry Pi! If you're looking for an easy and low cost way to get you digital sound files bumpin' then the MAX08357 I2S Amp Breakout is for you. It takes standard I2S digital audio input and, not only decodes it into analog, but also amplifies it directly into a speaker.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
  Rotary Encoder with Knob: Rotary Encoder with 1/4" Shaft and Knob
