# Fritzing sketch encoders_circuits (saved by Fritzing 0.9.3b)
breadboards: 1

parts:
  ENCODER1 = Rotary Encoder with Knob
  ENCODER2 = Rotary Encoder with Knob

nets:
  N1: ENCODER1.no_name_yet#5, ENCODER2.no_name_yet#4

custom parts:
  Rotary Encoder with Knob: Rotary Encoder with 1/4" Shaft and Knob
