# Fritzing sketch lcd_circuit (saved by Fritzing 0.9.3b)
breadboards: 1

parts:
  Part2 = TFT 1.8 inch 160x128 w microSD [part_number=358]

nets:
  N1: Part2.LITE, Part2.+5V

custom parts:
  TFT 1.8 inch 160x128 w microSD: This lovely little display breakout is the best way to add a small, colorful and bright display to any project. Since the display uses 4-wire SPI to communicate and has its own pixel-addressable frame buffer, it can be used with every kind of microcontroller. Even a very small one with low memory and few pins available! The 1.8" display has 128x160 color pixels.
